// Digital circuit PC.dig as structural Verilog
module PC (
  input  Clock,
  input  [1:0] Ctrl,
  input  [3:0] Load_Manual,
  output [3:0] Output
);

  wire [3:0] _4_bit_adder_v1_1_p3, multiplexer_1_out;

  // _4_bit_adder_v1 _4_bit_adder_v1_1: pin names not known; wires that end beside it: Output, 4'b0001, _4_bit_adder_v1_1_p3
  Multiplexer #(.Selector_Bits(2), .Bits(4)) multiplexer_1 (
    .sel(Ctrl), .in_0(Output), .in_1(_4_bit_adder_v1_1_p3), .in_2(Load_Manual), .in_3(4'b0000),
    .out(multiplexer_1_out));
  D_FF d_ff_1 (.D(multiplexer_1_out[3]), .C(Clock), .Q(Output[3]));  // open: nQ
  D_FF d_ff_2 (.D(multiplexer_1_out[2]), .C(Clock), .Q(Output[2]));  // open: nQ
  D_FF d_ff_3 (.D(multiplexer_1_out[1]), .C(Clock), .Q(Output[1]));  // open: nQ
  D_FF d_ff_4 (.D(multiplexer_1_out[0]), .C(Clock), .Q(Output[0]));  // open: nQ
  // Pins of 2 and 4 bits meet at Load_Manual
endmodule
