// Digital circuit Registers_DRAM.dig as structural Verilog
module Registers_DRAM (
  input  Clk,
  input  [1:0] MEM_CTRL__Read__Store__Reset,
  input  [1:0] IR_CTRL__Read__Store__Reset,
  input  [1:0] PC_CTRL__Read__Inc__Load__Reset,
  input  [3:0] PC_Load_Manual,
  input  MEM_ChipSelect,
  input  [1:0] GPR_CTRL__Read__Store__Reset,
  input  [1:0] GPR_Select,
  input  [3:0] GPR_manualinput,
  input  GPR_DataSelect__Manual_or_DRAM,
  input  MEM_DataSelect_Manual_or_GPR,
  input  [3:0] MEM_ManualInput,
  input  IR_DataSelect__Manual_or_DRAM,
  input  [3:0] IR_ManualInput,
  output [3:0] Output
);

  wire and_1_out, and_2_out, and_3_out, and_4_out, decoder_1_out_0, decoder_1_out_1, decoder_1_out_2,
       decoder_1_out_3, pc_1_p4;
  wire [3:0] memory_1_p6, multiplexer_1_out, multiplexer_2_out, multiplexer_3_out, multiplexer_4_out,
       R_0_output, R_1_output, R_2_output, R_3_output;

  Multiplexer #(.Bits(4)) multiplexer_1 (
    .sel(IR_DataSelect__Manual_or_DRAM), .in_0(IR_ManualInput), .in_1(memory_1_p6), .out(multiplexer_1_out));
  Multiplexer #(.Bits(4)) multiplexer_2 (
    .sel(MEM_DataSelect_Manual_or_GPR), .in_0(MEM_ManualInput), .in_1(multiplexer_4_out),
    .out(multiplexer_2_out));
  Decoder #(.Selector_Bits(2)) decoder_1 (
    .sel(GPR_Select), .out_0(decoder_1_out_0), .out_1(decoder_1_out_1), .out_2(decoder_1_out_2),
    .out_3(decoder_1_out_3));
  Multiplexer #(.Bits(4)) multiplexer_3 (
    .sel(GPR_DataSelect__Manual_or_DRAM), .in_0(GPR_manualinput), .in_1(memory_1_p6), .out(multiplexer_3_out));
  // PC pc_1: pin names not known; wires that end beside it: Clk, PC_CTRL__Read__Inc__Load__Reset, PC_Load_Manual, pc_1_p4
  and and_1 (and_1_out, decoder_1_out_0, Clk);
  and and_2 (and_2_out, decoder_1_out_1, Clk);
  and and_3 (and_3_out, decoder_1_out_2, Clk);
  and and_4 (and_4_out, decoder_1_out_3, Clk);
  GPR R_0 (
    .Ctrl__0_Read_1_Write_2_Reset(GPR_CTRL__Read__Store__Reset), .Clock(and_1_out),
    .Input(multiplexer_3_out), .Output(R_0_output));
  GPR R_1 (
    .Ctrl__0_Read_1_Write_2_Reset(GPR_CTRL__Read__Store__Reset), .Clock(and_2_out),
    .Input(multiplexer_3_out), .Output(R_1_output));
  GPR R_2 (
    .Ctrl__0_Read_1_Write_2_Reset(GPR_CTRL__Read__Store__Reset), .Clock(and_3_out),
    .Input(multiplexer_3_out), .Output(R_2_output));
  GPR R_3 (
    .Ctrl__0_Read_1_Write_2_Reset(GPR_CTRL__Read__Store__Reset), .Clock(and_4_out),
    .Input(multiplexer_3_out), .Output(R_3_output));
  // Memory memory_1: pin names not known; wires that end beside it: pc_1_p4, Clk, multiplexer_2_out, MEM_CTRL__Read__Store__Reset, MEM_ChipSelect, memory_1_p6
  Multiplexer #(.Bits(4), .Selector_Bits(2)) multiplexer_4 (
    .sel(GPR_Select), .in_0(R_0_output), .in_1(R_1_output), .in_2(R_2_output), .in_3(R_3_output),
    .out(multiplexer_4_out));
  // IR ir_1: pin names not known; wires that end beside it: IR_CTRL__Read__Store__Reset, Clk, multiplexer_1_out, Output
endmodule
